# Fritzing sketch light_table_contest-project (saved by Fritzing 0.9.3b)
perfboards: 1

parts:
  Componente1 = Arduino Nano (Rev3.0)
  VCC1 = Battery
  S1 = Pushbutton [package="[THT]"]
  S2 = Pushbutton [package="[THT]"]
  S3 = Pushbutton [package="[THT]"]
  LED1 = LED - 5mm [color="Red (633nm)" package="5 mm [THT]"]
  LED2 = LED - 5mm [color="Red (633nm)" package="5 mm [THT]"]
  LED3 = LED - 5mm [color="Red (633nm)" package="5 mm [THT]"]
  LED4 = LED - 5mm [color="Red (633nm)" package="5 mm [THT]"]
  LED5 = LED - 5mm [color="Red (633nm)" package="5 mm [THT]"]
  S4 = Pushbutton [package="[THT]"]
  S5 = Pushbutton [package="[THT]"]

nets:
  N1: Componente1.D2, Componente1.D3, Componente1.D4, S1.Pin_1, S1.Pin_2, S2.Pin_1, S2.Pin_2, S3.Pin_1, S3.Pin_2, S4.Pin_1, S4.Pin_2, S5.Pin_1, S5.Pin_2
  N2: Componente1.D5, S4.Pin_3, S4.Pin_4
  N3: Componente1.D6, S5.Pin_3, S5.Pin_4
  N4: Componente1.D7, LED1.cathode
  N5: Componente1.D8, LED2.cathode
  N6: Componente1.D9, LED3.cathode
  N7: Componente1.D10, LED4.cathode
  N8: Componente1.D11/MOSI, LED5.cathode
  N9: Componente1.5V, VCC1.+
  N10: VCC1.-, LED1.anode, LED2.anode, LED3.anode, LED4.anode, LED5.anode
  N11: S1.Pin_3, S1.Pin_4
  N12: S2.Pin_3, S2.Pin_4
  N13: S3.Pin_3, S3.Pin_4
